# Fritzing sketch menorah (saved by Fritzing 0.8.3b)
breadboards: 1

parts:
  TRINKET1 = Trinket 3V
  U1 = 74HC595 [package="DIP16 [THT]"]
  LED1 = LED - 5mm [color="Red (633nm)" package="5 mm [THT]"]
  LED2 = LED - 5mm [color="Red (633nm)" package="5 mm [THT]"]
  LED3 = LED - 5mm [color="Red (633nm)" package="5 mm [THT]"]
  LED4 = LED - 5mm [color="Red (633nm)" package="5 mm [THT]"]
  LED5 = LED - 5mm [color="Orange (620nm)" package="5 mm [THT]"]
  LED6 = LED - 5mm [color="Red (633nm)" package="5 mm [THT]"]
  LED7 = LED - 5mm [color="Red (633nm)" package="5 mm [THT]"]
  LED8 = LED - 5mm [color="Red (633nm)" package="5 mm [THT]"]
  LED9 = LED - 5mm [color="Red (633nm)" package="5 mm [THT]"]
  S1 = Pushbutton [package=THT]
  R1 = Resistor [tolerance=±5% resistance=220 package=THT]

nets:
  N1: TRINKET1.no_name_yet#2, U1.GND, U1.OE, LED1.cathode, LED2.cathode, LED3.cathode, LED4.cathode, LED5.cathode, LED6.cathode, LED7.cathode, LED8.cathode, LED9.cathode
  N2: TRINKET1.no_name_yet#3, S1.leg1
  N3: TRINKET1.no_name_yet#4, S1.leg0
  N4: TRINKET1.no_name_yet#6, U1.MR, U1.VCC, R1.Pin_1
  N5: TRINKET1.no_name_yet#7, U1.DS
  N6: TRINKET1.no_name_yet#8, U1.ST_CP
  N7: TRINKET1.no_name_yet#9, U1.SH_CP
  N8: U1.Q1, LED2.anode
  N9: U1.Q2, LED3.anode
  N10: U1.Q3, LED4.anode
  N11: U1.Q4, LED6.anode
  N12: U1.Q5, LED7.anode
  N13: U1.Q6, LED8.anode
  N14: U1.Q7, LED9.anode
  N15: U1.Q0, LED1.anode
  N16: LED5.anode, R1.Pin_0

custom parts:
  Trinket 3V: Adafruit Trinket 3V
